# Fritzing sketch Breadboard (saved by Fritzing 0.9.4)
circuit board: 7.79967cm x 4.65148cm
breadboards: 1

parts:
  WiFi = ESP8266 WiFi Module [part_number=ESP8266]
  220OHM = Resistor [tolerance=±5% resistance=220 package=THT]
  220ohm = Resistor [tolerance=±5% resistance=220 package=THT]
  220ohm_2 = Resistor [tolerance=±5% resistance=220 package=THT]
  Arduino = Arduino Nano (Rev3.0)
  LD1117V33 = V_REG_LD1117VXX [package=78xxl]
  LD1117V50 = Voltage Regulator [package=78xxl]
  100nf = Electrolytic Capacitor [capacitance=100nF package="100 mil [THT, electrolytic]"]
  10uf = Electrolytic Capacitor [capacitance=10µF package="100 mil [THT, electrolytic]"]
  100nf_2 = Electrolytic Capacitor [capacitance=100nF package="100 mil [THT, electrolytic]"]
  10uf_2 = Electrolytic Capacitor [capacitance=10µF package="100 mil [THT, electrolytic]"]
  BME280 = female pin header, 4 pins [form="♀ (female)"]
  Display = female pin header, 4 pins [form="♀ (female)"]
  9V = Battery block 9V
  9v = Power Jack [package=power_jack_pth]

nets:
  N1: WiFi.RXD, 220ohm.Pin_1, 220ohm_2.Pin_0
  N2: WiFi.VCC, WiFi.CH_PD, LD1117V33.OUT, 10uf.+
  GND: WiFi.GND, 220OHM.Pin_0, Arduino.GND, LD1117V33.GND, LD1117V50.IN, 100nf.-, 10uf.-, 100nf_2.-, 10uf_2.-, BME280.pin3, Display.pin4, 9V.-, 9v.GND
  N3: WiFi.TXD, Arduino.D6
  N4: 220OHM.Pin_1, 220ohm.Pin_0
  N5: 220ohm_2.Pin_1, Arduino.D7
  N6: Arduino.VIN, LD1117V33.IN, LD1117V50.OUT, 100nf.+, 100nf_2.+, 9V.+, 9v.PWR
  N7: Arduino.A5, BME280.pin2, Display.pin2
  N8: Arduino.A4, BME280.pin1, Display.pin1
  N9: LD1117V50.GND, 10uf_2.+, BME280.pin4, Display.pin3

notes:
  Environment Monitor v1
  Designed by Sam Pratt
  5v GND SCL SDA
  SDA SCL 5v GND
  + -
  GND
  PWR
  RX TX
  SCL SDA
  VIN GND
  GND      RX
  TX EN  VCC

custom parts:
  ESP8266 WiFi Module: Generic WiFi Module based on the ESP8266 with onboard PCB antenna and UART communications
